# Fritzing sketch main_board (saved by Fritzing 0.8.0b)
breadboards: 1

parts:
  Arduino1 = Arduino
  R2 = Resistor [tolerance=±5% resistance=10k package=THT]
  LED1 = white LED - 5mm
  LED3 = white LED - 5mm
  LED4 = white LED - 5mm
  LED5 = white LED - 5mm
  LED6 = white LED - 5mm
  LED7 = white LED - 5mm
  LED8 = white LED - 5mm
  L1 = Solenoid
  Q1 = Basic FET P-Channel [package="TO220 [THT]"]
  D1 = Rectifier Diode [part_number=1N4001 package="300 mil [THT]"]
  S1 = Round Pushbutton
  U1 = Packages: [package=tssop28-groundpad]  # not connected
  R3 = Resistor [tolerance=±5% resistance=1k package=THT]  # not connected
  C1 = Electrolytic Capacitor [capacitance=0.1mF voltage=50V package="100 mil [THT, electrolytic]"]
  R4 = Resistor [tolerance=±5% resistance=2.2k package=THT]
  S2 = Reed switch [package=THT]
  R5 = Resistor [tolerance=±5% resistance=10k package=THT]
  U3 = XBEE-1 [package=xbee-1_lock]
  LED2 = white LED - 5mm
  U4 = mystery part, 14 pins [chip_label=TLC594ONT]

nets:
  GND: Arduino1.GND, LED1.anode, LED3.anode, LED4.anode, LED5.anode, LED6.anode, LED7.anode, LED8.anode, Q1.source, S1.leg1, C1.+, S2.pin_2, R5.Pin_1, U3.GND, LED2.anode
  N1: Arduino1.D7, Q1.gate
  N2: Arduino1.D6, S2.pin_1, R5.Pin_0
  N3: Arduino1.D5, R2.Pin_1, S1.leg0
  N4: Arduino1.D1TX, U3.DIN
  N5: Arduino1.D0RX, U3.DOUT
  3V3: Arduino1.3V3, U3.VDD
  N6: Arduino1.+5V, R2.Pin_0, C1.-, R4.Pin_0
  N7: Arduino1.VIN, L1.pin2, D1.cathode
  N8: LED1.cathode, U4.pin7
  N9: LED3.cathode, U4.pin6
  N10: LED4.cathode, U4.pin5
  N11: LED5.cathode, U4.pin4
  N12: LED6.cathode, U4.pin3
  N13: LED7.cathode, U4.pin2
  N14: LED8.cathode, U4.pin1
  N15: L1.pin1, Q1.drain, D1.anode
  N16: LED2.cathode, U4.pin8

notes:
  10K
  1K
  2K
  change the resistor to 2.2k or 3.2k etc to reduce load into driver
